# Fritzing sketch Conexion_FTDI (saved by Fritzing 1.0.1rc)
breadboards: 1

parts:
  A1 = FT232-AZ USB to TTL serial adapter
  U1 = 74HC04_HEX_INVERTER [package=dil14]
  CN1 = DB9

nets:
  N1: A1.Pin_8, A1.Pin_9, A1.Pin_19
  N2: U1.1A, CN1.2_RXD
  N3: U1.GND, CN1.5_GND
  N4: U1.VCC, CN1.3_TXD

custom parts:
  FT232-AZ USB to TTL serial adapter: FT232-AZ USB to TTL serial adapter.
  DB9: RS232 connector, 9-pin, right-angle female. Minimum connections is RXD, TXD, GND
